// Logisim project 2.circ as structural Verilog: 1 circuit, main circuit main
module main (
  output [18:0] _2,
  output [18:0] out_2,
  output [18:0] out_3,
  output [18:0] out_4,
  output [18:0] out_5,
  output [18:0] out_6,
  output [18:0] out_7,
  output [18:0] out_8,
  output [18:0] out_9,
  output [18:0] out_10,
  output [18:0] out_11,
  output [18:0] out_12,
  output [18:0] out_13,
  output [18:0] out_14,
  output [18:0] out_15,
  output [18:0] out_16,
  output [18:0] out_17,
  output [18:0] out_18,
  output [18:0] out_19
);


  assign _2 = {19{1'b0}};
  assign out_2 = {19{1'b0}};
  assign out_3 = {19{1'b0}};
  assign out_4 = {19{1'b0}};
  assign out_5 = {19{1'b0}};
  assign out_6 = 19'h10;
  assign out_7 = 19'h3030;
  assign out_8 = 19'h4050;
  assign out_9 = 19'h8090;
  assign out_10 = 19'h8110;
  assign out_11 = 19'h8210;
  assign out_12 = 19'h4410;
  assign out_13 = 19'h7810;
  assign out_14 = 19'h10;
  assign out_15 = {19{1'b0}};
  assign out_16 = {19{1'b0}};
  assign out_17 = {19{1'b0}};
  assign out_18 = {19{1'b0}};
  assign out_19 = {19{1'b0}};
endmodule
