// Logisim project main.circ as structural Verilog: 3 circuits, main circuit random
module main (
);

  wire and_1_out, cdm16_1_p3, cdm16_1_p10, cdm16_1_p12, cdm16_1_p14, clock_1_out, clock_3_out, clock_4_out,
       comparator_1_eq, enable_matrix, mem, not_1_out, not_2_out, not_3_out, read, small_comparator_1_out_3,
       small_comparator_2_out_3, small_comparator_3_out_3, small_comparator_4_out_3,
       small_comparator_5_out_3, small_comparator_6_out_3, small_comparator_7_out_3,
       small_comparator_8_out_3, small_comparator_9_out_3, small_comparator_10_out_3,
       small_comparator_11_out_3, small_comparator_12_out_3, small_comparator_13_out_3,
       small_comparator_14_out_3, small_comparator_15_out_3, small_comparator_16_out_3,
       small_comparator_17_out_3, word;
  wire [3:0] _0_i, _0_o, _1_i, _1_o, _2_i, _2_o, _3_i, _3_o, _4_i, _4_o, _5_i, _5_o, _6_i, _6_o, _7_i, _7_o,
       _8_i, _8_o, _9_i, _9_o, _10_i, _10_o, _11_i, _11_o, _12_i, _12_o, _13_i, _13_o, _14_i, _14_o, _15_i,
       _15_o, bitselector_3_out, bitselector_4_out;
  wire [4:0] bitselector_2_out;
  wire [7:0] bitselector_1_out;
  wire [15:0] address_bus, cdm16_1_p20, cdm16_1_p21, data, data_bus, r0, r1, r2, r3, r4, r5, r6, r7,
       random_1_out_2;
  wire [18:0] main_1_out_2, main_1_out_3, main_1_out_4, main_1_out_5, main_1_out_6, main_1_out_7,
       main_1_out_8, main_1_out_9, main_1_out_10, main_1_out_11, main_1_out_12, main_1_out_13, main_1_out_14,
       main_1_out_15, main_1_out_16, main_1_out_17, main_1_out_18, main_1_out_19, main_1_out_20,
       main_2_out_2, main_2_out_3, main_2_out_4, main_2_out_5, main_2_out_6, main_2_out_7, main_2_out_8,
       main_2_out_9, main_2_out_10, main_2_out_11, main_2_out_12, main_2_out_13, main_2_out_14,
       main_2_out_15, main_2_out_16, main_2_out_17, main_2_out_18, main_2_out_19, main_2_out_20,
       main_3_out_2, main_3_out_3, main_3_out_4, main_3_out_5, main_3_out_6, main_3_out_7, main_3_out_8,
       main_3_out_9, main_3_out_10, main_3_out_11, main_3_out_12, main_3_out_13, main_3_out_14,
       main_3_out_15, main_3_out_16, main_3_out_17, main_3_out_18, main_3_out_19, main_3_out_20,
       main_4_out_2, main_4_out_3, main_4_out_4, main_4_out_5, main_4_out_6, main_4_out_7, main_4_out_8,
       main_4_out_9, main_4_out_10, main_4_out_11, main_4_out_12, main_4_out_13, main_4_out_14,
       main_4_out_15, main_4_out_16, main_4_out_17, main_4_out_18, main_4_out_19, main_4_out_20,
       main_5_out_2, main_5_out_3, main_5_out_4, main_5_out_5, main_5_out_6, main_5_out_7, main_5_out_8,
       main_5_out_9, main_5_out_10, main_5_out_11, main_5_out_12, main_5_out_13, main_5_out_14,
       main_5_out_15, main_5_out_16, main_5_out_17, main_5_out_18, main_5_out_19, main_5_out_20,
       main_6_out_2, main_6_out_3, main_6_out_4, main_6_out_5, main_6_out_6, main_6_out_7, main_6_out_8,
       main_6_out_9, main_6_out_10, main_6_out_11, main_6_out_12, main_6_out_13, main_6_out_14,
       main_6_out_15, main_6_out_16, main_6_out_17, main_6_out_18, main_6_out_19, main_6_out_20,
       main_7_out_2, main_7_out_3, main_7_out_4, main_7_out_5, main_7_out_6, main_7_out_7, main_7_out_8,
       main_7_out_9, main_7_out_10, main_7_out_11, main_7_out_12, main_7_out_13, main_7_out_14,
       main_7_out_15, main_7_out_16, main_7_out_17, main_7_out_18, main_7_out_19, main_7_out_20,
       main_8_out_2, main_8_out_3, main_8_out_4, main_8_out_5, main_8_out_6, main_8_out_7, main_8_out_8,
       main_8_out_9, main_8_out_10, main_8_out_11, main_8_out_12, main_8_out_13, main_8_out_14,
       main_8_out_15, main_8_out_16, main_8_out_17, main_8_out_18, main_8_out_19, main_8_out_20,
       main_9_out_2, main_9_out_3, main_9_out_4, main_9_out_5, main_9_out_6, main_9_out_7, main_9_out_8,
       main_9_out_9, main_9_out_10, main_9_out_11, main_9_out_12, main_9_out_13, main_9_out_14,
       main_9_out_15, main_9_out_16, main_9_out_17, main_9_out_18, main_9_out_19, main_9_out_20,
       main_10_out_2, main_10_out_3, main_10_out_4, main_10_out_5, main_10_out_6, main_10_out_7,
       main_10_out_8, main_10_out_9, main_10_out_10, main_10_out_11, main_10_out_12, main_10_out_13,
       main_10_out_14, main_10_out_15, main_10_out_16, main_10_out_17, main_10_out_18, main_10_out_19,
       main_10_out_20, main_11_out_2, main_11_out_3, main_11_out_4, main_11_out_5, main_11_out_6,
       main_11_out_7, main_11_out_8, main_11_out_9, main_11_out_10, main_11_out_11, main_11_out_12,
       main_11_out_13, main_11_out_14, main_11_out_15, main_11_out_16, main_11_out_17, main_11_out_18,
       main_11_out_19, main_11_out_20, main_12_out_2, main_12_out_3, main_12_out_4, main_12_out_5,
       main_12_out_6, main_12_out_7, main_12_out_8, main_12_out_9, main_12_out_10, main_12_out_11,
       main_12_out_12, main_12_out_13, main_12_out_14, main_12_out_15, main_12_out_16, main_12_out_17,
       main_12_out_18, main_12_out_19, main_12_out_20, main_13_out_2, main_13_out_3, main_13_out_4,
       main_13_out_5, main_13_out_6, main_13_out_7, main_13_out_8, main_13_out_9, main_13_out_10,
       main_13_out_11, main_13_out_12, main_13_out_13, main_13_out_14, main_13_out_15, main_13_out_16,
       main_13_out_17, main_13_out_18, main_13_out_19, main_13_out_20, main_14_out_2, main_14_out_3,
       main_14_out_4, main_14_out_5, main_14_out_6, main_14_out_7, main_14_out_8, main_14_out_9,
       main_14_out_10, main_14_out_11, main_14_out_12, main_14_out_13, main_14_out_14, main_14_out_15,
       main_14_out_16, main_14_out_17, main_14_out_18, main_14_out_19, main_14_out_20, main_15_out_2,
       main_15_out_3, main_15_out_4, main_15_out_5, main_15_out_6, main_15_out_7, main_15_out_8,
       main_15_out_9, main_15_out_10, main_15_out_11, main_15_out_12, main_15_out_13, main_15_out_14,
       main_15_out_15, main_15_out_16, main_15_out_17, main_15_out_18, main_15_out_19, main_15_out_20,
       main_16_out_2, main_16_out_3, main_16_out_4, main_16_out_5, main_16_out_6, main_16_out_7,
       main_16_out_8, main_16_out_9, main_16_out_10, main_16_out_11, main_16_out_12, main_16_out_13,
       main_16_out_14, main_16_out_15, main_16_out_16, main_16_out_17, main_16_out_18, main_16_out_19,
       main_16_out_20, undriven;

  random random_1 (.in_1(clock_1_out), .out_2(random_1_out_2));
  Clock clock_1 (.out(clock_1_out));
  // cdm16 cdm16_1: pin names not known; wires that end beside it: r0, r1, cdm16_1_p3, r2, r3, r4, r5, r6, r7, cdm16_1_p10, cdm16_1_p10, cdm16_1_p12, cdm16_1_p12, cdm16_1_p14, cdm16_1_p14, mem, read, word, address_bus, cdm16_1_p20, cdm16_1_p21
  Clock clock_2 (.out(cdm16_1_p3));
  Clock clock_3 (.out(clock_3_out));
  BitSelector #(.width(16), .group(8)) bitselector_1 (.in(address_bus), .out(bitselector_1_out), .sel(1'b1));
  not not_1 (not_1_out, read);
  BitSelector #(.width(16), .group(5)) bitselector_2 (.in(address_bus), .out(bitselector_2_out), .sel(2'b00));
  Multiplexer #(.width(16), .enable("false")) multiplexer_1 (
    .in0(data_bus), .in1(random_1_out_2), .out(data), .sel(comparator_1_eq));
  Comparator #(.width(16)) comparator_1 (
    .a(16'hfefe), .b(address_bus), .gt(enable_matrix), .eq(comparator_1_eq));  // open: lt
  and and_1 (and_1_out, bitselector_1_out[0], bitselector_1_out[1], bitselector_1_out[2], bitselector_1_out[3], bitselector_1_out[4], bitselector_1_out[6], bitselector_1_out[7], bitselector_1_out[5], not_1_out, not_2_out);
  not not_2 (not_2_out, small_comparator_17_out_3);
  assign data_bus = not_3_out ? cdm16_1_p20 : 16'bz;  // Controlled_Buffer controlled_buffer_1
  not not_3 (not_3_out, read);
  Controlled_Buffer #(.width(16)) controlled_buffer_2 (.in(data_bus), .en(read));  // open: out
  assign cdm16_1_p21 = read ? data : 16'bz;  // Controlled_Buffer controlled_buffer_3
  small_comparator small_comparator_1 (.in_1(4'b0000), .in_2(bitselector_2_out[4:1]), .out_3(small_comparator_1_out_3));
  small_comparator small_comparator_2 (.in_1(4'b0001), .in_2(bitselector_2_out[4:1]), .out_3(small_comparator_2_out_3));
  small_comparator small_comparator_3 (.in_1(4'b0010), .in_2(bitselector_2_out[4:1]), .out_3(small_comparator_3_out_3));
  small_comparator small_comparator_4 (.in_1(4'b0011), .in_2(bitselector_2_out[4:1]), .out_3(small_comparator_4_out_3));
  small_comparator small_comparator_5 (.in_1(4'b0100), .in_2(bitselector_2_out[4:1]), .out_3(small_comparator_5_out_3));
  small_comparator small_comparator_6 (.in_1(4'b0101), .in_2(bitselector_2_out[4:1]), .out_3(small_comparator_6_out_3));
  small_comparator small_comparator_7 (.in_1(4'b0110), .in_2(bitselector_2_out[4:1]), .out_3(small_comparator_7_out_3));
  small_comparator small_comparator_8 (.in_1(4'b0111), .in_2(bitselector_2_out[4:1]), .out_3(small_comparator_8_out_3));
  small_comparator small_comparator_9 (.in_1(4'b1000), .in_2(bitselector_2_out[4:1]), .out_3(small_comparator_9_out_3));
  small_comparator small_comparator_10 (
    .in_1(4'b1001), .in_2(bitselector_2_out[4:1]), .out_3(small_comparator_10_out_3));
  small_comparator small_comparator_11 (
    .in_1(4'b1010), .in_2(bitselector_2_out[4:1]), .out_3(small_comparator_11_out_3));
  small_comparator small_comparator_12 (
    .in_1(4'b1011), .in_2(bitselector_2_out[4:1]), .out_3(small_comparator_12_out_3));
  small_comparator small_comparator_13 (
    .in_1(4'b1100), .in_2(bitselector_2_out[4:1]), .out_3(small_comparator_13_out_3));
  small_comparator small_comparator_14 (
    .in_1(4'b1101), .in_2(bitselector_2_out[4:1]), .out_3(small_comparator_14_out_3));
  small_comparator small_comparator_15 (
    .in_1(4'b1110), .in_2(bitselector_2_out[4:1]), .out_3(small_comparator_15_out_3));
  small_comparator small_comparator_16 (
    .in_1(4'b1111), .in_2(bitselector_2_out[4:1]), .out_3(small_comparator_16_out_3));
  BitSelector #(.width(16), .group(4)) bitselector_3 (.in(data_bus), .out(bitselector_3_out), .sel(2'b11));
  small_comparator small_comparator_17 (.in_1(bitselector_3_out), .in_2(4'b1111), .out_3(small_comparator_17_out_3));
  Demultiplexer #(.select(4), .width(4)) demultiplexer_1 (
    .out0(_0_i), .out1(_1_i), .out2(_2_i), .out3(_3_i), .out4(_4_i), .out5(_5_i), .out6(_6_i), .out7(_7_i),
    .out8(_8_i), .out9(_9_i), .out10(_10_i), .out11(_11_i), .out12(_12_i), .out13(_13_i), .out14(_14_i),
    .out15(_15_i), .in(bitselector_4_out), .sel(bitselector_2_out[4:1]), .en(and_1_out));
  BitSelector #(.width(16), .group(4)) bitselector_4 (.in(data_bus), .out(bitselector_4_out), .sel(2'b00));
  Clock clock_4 (.out(clock_4_out));
  Register #(.width(4)) register_1 (.D(_0_i), .en(small_comparator_1_out_3), .Q(_0_o), .clk(clock_3_out));  // open: clr
  Register #(.width(4)) register_2 (.D(_4_i), .en(small_comparator_5_out_3), .Q(_4_o), .clk(clock_3_out));  // open: clr
  Register #(.width(4)) register_3 (.D(_8_i), .en(small_comparator_9_out_3), .Q(_8_o), .clk(clock_3_out));  // open: clr
  Register #(.width(4)) register_4 (
    .D(_12_i), .en(small_comparator_13_out_3), .Q(_12_o), .clk(clock_3_out));  // open: clr
  // Debugger debugger_1: pin names not known
  // RAM ram_1: pin names not known; wires that end beside it: address_bus, word, mem, clock_4_out, read, data_bus
  Register #(.width(4)) register_5 (.D(_1_i), .en(small_comparator_2_out_3), .Q(_1_o), .clk(clock_3_out));  // open: clr
  Register #(.width(4)) register_6 (.D(_5_i), .en(small_comparator_6_out_3), .Q(_5_o), .clk(clock_3_out));  // open: clr
  Register #(.width(4)) register_7 (
    .D(_9_i), .en(small_comparator_10_out_3), .Q(_9_o), .clk(clock_3_out));  // open: clr
  Register #(.width(4)) register_8 (
    .D(_13_i), .en(small_comparator_14_out_3), .Q(_13_o), .clk(clock_3_out));  // open: clr
  Register #(.width(4)) register_9 (.D(_2_i), .en(small_comparator_3_out_3), .Q(_2_o), .clk(clock_3_out));  // open: clr
  Register #(.width(4)) register_10 (
    .D(_6_i), .en(small_comparator_7_out_3), .Q(_6_o), .clk(clock_3_out));  // open: clr
  Register #(.width(4)) register_11 (
    .D(_10_i), .en(small_comparator_11_out_3), .Q(_10_o), .clk(clock_3_out));  // open: clr
  Register #(.width(4)) register_12 (
    .D(_14_i), .en(small_comparator_15_out_3), .Q(_14_o), .clk(clock_3_out));  // open: clr
  DotMatrix #(.matrixcols(19), .matrixrows(19)) dotmatrix_1 (
    .col0({19{1'b1}}), .col1({19{1'b1}}), .col2({19{1'b1}}), .col3({19{1'b1}}), .col4({19{1'b0}}),
    .col5({19{1'b1}}), .col6({19{1'b1}}), .col7({19{1'b1}}), .col8({19{1'b1}}), .col9({19{1'b0}}),
    .col10({19{1'b1}}), .col11({19{1'b1}}), .col12({19{1'b1}}), .col13({19{1'b1}}), .col14({19{1'b0}}),
    .col15({19{1'b1}}), .col16({19{1'b1}}), .col17({19{1'b1}}), .col18({19{1'b1}}));
  Hex_Digit_Display hex_digit_display_1 ();  // open: value, dp
  Register #(.width(4)) register_13 (
    .D(_3_i), .en(small_comparator_4_out_3), .Q(_3_o), .clk(clock_3_out));  // open: clr
  Register #(.width(4)) register_14 (
    .D(_7_i), .en(small_comparator_8_out_3), .Q(_7_o), .clk(clock_3_out));  // open: clr
  Register #(.width(4)) register_15 (
    .D(_11_i), .en(small_comparator_12_out_3), .Q(_11_o), .clk(clock_3_out));  // open: clr
  Register #(.width(4)) register_16 (
    .D(_15_i), .en(small_comparator_16_out_3), .Q(_15_o), .clk(clock_3_out));  // open: clr
  Hex_Digit_Display hex_digit_display_2 ();  // open: value, dp
  Hex_Digit_Display hex_digit_display_3 ();  // open: value, dp
  Hex_Digit_Display hex_digit_display_4 ();  // open: value, dp
  DotMatrix #(.matrixcols(19), .matrixrows(19)) dotmatrix_2 (
    .col0(main_1_out_2), .col1(main_1_out_6), .col2(main_1_out_10), .col3(main_1_out_14),
    .col4(main_1_out_18), .col5(main_1_out_3), .col6(main_1_out_7), .col7(main_1_out_11),
    .col8(main_1_out_15), .col9(main_1_out_19), .col10(main_1_out_4), .col11(main_1_out_8),
    .col12(main_1_out_12), .col13(main_1_out_16), .col14(main_1_out_20), .col15(main_1_out_5),
    .col16(main_1_out_9), .col17(main_1_out_13), .col18(main_1_out_17));
  number_picker_main main_1 (
    .in_1(_0_o), .out_2(main_1_out_2), .out_3(main_1_out_3), .out_4(main_1_out_4), .out_5(main_1_out_5),
    .out_6(main_1_out_6), .out_7(main_1_out_7), .out_8(main_1_out_8), .out_9(main_1_out_9),
    .out_10(main_1_out_10), .out_11(main_1_out_11), .out_12(main_1_out_12), .out_13(main_1_out_13),
    .out_14(main_1_out_14), .out_15(main_1_out_15), .out_16(main_1_out_16), .out_17(main_1_out_17),
    .out_18(main_1_out_18), .out_19(main_1_out_19), .out_20(main_1_out_20));
  number_picker_main main_2 (
    .in_1(_4_o), .out_2(main_2_out_2), .out_3(main_2_out_3), .out_4(main_2_out_4), .out_5(main_2_out_5),
    .out_6(main_2_out_6), .out_7(main_2_out_7), .out_8(main_2_out_8), .out_9(main_2_out_9),
    .out_10(main_2_out_10), .out_11(main_2_out_11), .out_12(main_2_out_12), .out_13(main_2_out_13),
    .out_14(main_2_out_14), .out_15(main_2_out_15), .out_16(main_2_out_16), .out_17(main_2_out_17),
    .out_18(main_2_out_18), .out_19(main_2_out_19), .out_20(main_2_out_20));
  DotMatrix #(.matrixcols(19), .matrixrows(19)) dotmatrix_3 (
    .col0(main_2_out_2), .col1(main_2_out_6), .col2(main_2_out_10), .col3(main_2_out_14),
    .col4(main_2_out_18), .col5(main_2_out_3), .col6(main_2_out_7), .col7(main_2_out_11),
    .col8(main_2_out_15), .col9(main_2_out_19), .col10(main_2_out_4), .col11(main_2_out_8),
    .col12(main_2_out_12), .col13(main_2_out_16), .col14(main_2_out_20), .col15(main_2_out_5),
    .col16(main_2_out_9), .col17(main_2_out_13), .col18(main_2_out_17));
  number_picker_main main_3 (
    .in_1(_8_o), .out_2(main_3_out_2), .out_3(main_3_out_3), .out_4(main_3_out_4), .out_5(main_3_out_5),
    .out_6(main_3_out_6), .out_7(main_3_out_7), .out_8(main_3_out_8), .out_9(main_3_out_9),
    .out_10(main_3_out_10), .out_11(main_3_out_11), .out_12(main_3_out_12), .out_13(main_3_out_13),
    .out_14(main_3_out_14), .out_15(main_3_out_15), .out_16(main_3_out_16), .out_17(main_3_out_17),
    .out_18(main_3_out_18), .out_19(main_3_out_19), .out_20(main_3_out_20));
  DotMatrix #(.matrixcols(19), .matrixrows(19)) dotmatrix_4 (
    .col0(main_3_out_2), .col1(main_3_out_6), .col2(main_3_out_10), .col3(main_3_out_14),
    .col4(main_3_out_18), .col5(main_3_out_3), .col6(main_3_out_7), .col7(main_3_out_11),
    .col8(main_3_out_15), .col9(main_3_out_19), .col10(main_3_out_4), .col11(main_3_out_8),
    .col12(main_3_out_12), .col13(main_3_out_16), .col14(main_3_out_20), .col15(main_3_out_5),
    .col16(main_3_out_9), .col17(main_3_out_13), .col18(main_3_out_17));
  number_picker_main main_4 (
    .out_2(main_4_out_2), .out_3(main_4_out_3), .out_4(main_4_out_4), .out_5(main_4_out_5),
    .out_6(main_4_out_6), .out_7(main_4_out_7), .out_8(main_4_out_8), .out_9(main_4_out_9),
    .out_10(main_4_out_10), .out_11(main_4_out_11), .out_12(main_4_out_12), .out_13(main_4_out_13),
    .out_14(main_4_out_14), .out_15(main_4_out_15), .out_16(main_4_out_16), .out_17(main_4_out_17),
    .out_18(main_4_out_18), .out_19(main_4_out_19), .out_20(main_4_out_20));  // open: in_1
  DotMatrix #(.matrixcols(19), .matrixrows(19)) dotmatrix_5 (
    .col0(main_4_out_2), .col1(main_4_out_6), .col2(main_4_out_10), .col3(main_4_out_14),
    .col4(main_4_out_18), .col5(main_4_out_3), .col6(main_4_out_7), .col7(main_4_out_11),
    .col8(main_4_out_15), .col9(main_4_out_19), .col10(main_4_out_4), .col11(main_4_out_8),
    .col12(main_4_out_12), .col13(main_4_out_16), .col14(main_4_out_20), .col15(main_4_out_5),
    .col16(main_4_out_9), .col17(main_4_out_13), .col18(main_4_out_17));
  Hex_Digit_Display hex_digit_display_5 ();  // open: value, dp
  number_picker_main main_5 (
    .in_1(_1_o), .out_2(main_5_out_2), .out_3(main_5_out_3), .out_4(main_5_out_4), .out_5(main_5_out_5),
    .out_6(main_5_out_6), .out_7(main_5_out_7), .out_8(main_5_out_8), .out_9(main_5_out_9),
    .out_10(main_5_out_10), .out_11(main_5_out_11), .out_12(main_5_out_12), .out_13(main_5_out_13),
    .out_14(main_5_out_14), .out_15(main_5_out_15), .out_16(main_5_out_16), .out_17(main_5_out_17),
    .out_18(main_5_out_18), .out_19(main_5_out_19), .out_20(main_5_out_20));
  DotMatrix #(.matrixcols(19), .matrixrows(19)) dotmatrix_6 (
    .col0(main_5_out_2), .col1(main_5_out_6), .col2(main_5_out_10), .col3(main_5_out_14),
    .col4(main_5_out_18), .col5(main_5_out_3), .col6(main_5_out_7), .col7(main_5_out_11),
    .col8(main_5_out_15), .col9(main_5_out_19), .col10(main_5_out_4), .col11(main_5_out_8),
    .col12(main_5_out_12), .col13(main_5_out_16), .col14(main_5_out_20), .col15(main_5_out_5),
    .col16(main_5_out_9), .col17(main_5_out_13), .col18(main_5_out_17));
  number_picker_main main_6 (
    .in_1(_5_o), .out_2(main_6_out_2), .out_3(main_6_out_3), .out_4(main_6_out_4), .out_5(main_6_out_5),
    .out_6(main_6_out_6), .out_7(main_6_out_7), .out_8(main_6_out_8), .out_9(main_6_out_9),
    .out_10(main_6_out_10), .out_11(main_6_out_11), .out_12(main_6_out_12), .out_13(main_6_out_13),
    .out_14(main_6_out_14), .out_15(main_6_out_15), .out_16(main_6_out_16), .out_17(main_6_out_17),
    .out_18(main_6_out_18), .out_19(main_6_out_19), .out_20(main_6_out_20));
  DotMatrix #(.matrixcols(19), .matrixrows(19)) dotmatrix_7 (
    .col0(main_6_out_2), .col1(main_6_out_6), .col2(main_6_out_10), .col3(main_6_out_14),
    .col4(main_6_out_18), .col5(main_6_out_3), .col6(main_6_out_7), .col7(main_6_out_11),
    .col8(main_6_out_15), .col9(main_6_out_19), .col10(main_6_out_4), .col11(main_6_out_8),
    .col12(main_6_out_12), .col13(main_6_out_16), .col14(main_6_out_20), .col15(main_6_out_5),
    .col16(main_6_out_9), .col17(main_6_out_13), .col18(main_6_out_17));
  number_picker_main main_7 (
    .in_1(_9_o), .out_2(main_7_out_2), .out_3(main_7_out_3), .out_4(main_7_out_4), .out_5(main_7_out_5),
    .out_6(main_7_out_6), .out_7(main_7_out_7), .out_8(main_7_out_8), .out_9(main_7_out_9),
    .out_10(main_7_out_10), .out_11(main_7_out_11), .out_12(main_7_out_12), .out_13(main_7_out_13),
    .out_14(main_7_out_14), .out_15(main_7_out_15), .out_16(main_7_out_16), .out_17(main_7_out_17),
    .out_18(main_7_out_18), .out_19(main_7_out_19), .out_20(main_7_out_20));
  DotMatrix #(.matrixcols(19), .matrixrows(19)) dotmatrix_8 (
    .col0(main_7_out_2), .col1(main_7_out_6), .col2(main_7_out_10), .col3(main_7_out_14),
    .col4(main_7_out_18), .col5(main_7_out_3), .col6(main_7_out_7), .col7(main_7_out_11),
    .col8(main_7_out_15), .col9(main_7_out_19), .col10(main_7_out_4), .col11(main_7_out_8),
    .col12(main_7_out_12), .col13(main_7_out_16), .col14(main_7_out_20), .col15(main_7_out_5),
    .col16(main_7_out_9), .col17(main_7_out_13), .col18(main_7_out_17));
  DotMatrix #(.matrixcols(19), .matrixrows(19)) dotmatrix_9 (
    .col0(main_8_out_2), .col1(main_8_out_6), .col2(main_8_out_10), .col3(main_8_out_14),
    .col4(main_8_out_18), .col5(main_8_out_3), .col6(main_8_out_7), .col7(main_8_out_11),
    .col8(main_8_out_15), .col9(main_8_out_19), .col10(main_8_out_4), .col11(main_8_out_8),
    .col12(main_8_out_12), .col13(main_8_out_16), .col14(main_8_out_20), .col15(main_8_out_5),
    .col16(main_8_out_9), .col17(main_8_out_13), .col18(main_8_out_17));
  number_picker_main main_8 (
    .out_2(main_8_out_2), .out_3(main_8_out_3), .out_4(main_8_out_4), .out_5(main_8_out_5),
    .out_6(main_8_out_6), .out_7(main_8_out_7), .out_8(main_8_out_8), .out_9(main_8_out_9),
    .out_10(main_8_out_10), .out_11(main_8_out_11), .out_12(main_8_out_12), .out_13(main_8_out_13),
    .out_14(main_8_out_14), .out_15(main_8_out_15), .out_16(main_8_out_16), .out_17(main_8_out_17),
    .out_18(main_8_out_18), .out_19(main_8_out_19), .out_20(main_8_out_20));  // open: in_1
  // Probe on 19'hf80
  DotMatrix #(.matrixcols(19), .matrixrows(19)) dotmatrix_10 (
    .col0(19'hf80), .col1(19'h1040), .col2(19'h1040), .col3(19'hf80), .col4({19{1'b0}}), .col5(undriven),
    .col6(undriven), .col7(undriven), .col8(undriven), .col9({19{1'b0}}), .col10(undriven), .col11(undriven),
    .col12(undriven), .col13(undriven), .col14({19{1'b0}}), .col15(undriven), .col16(undriven),
    .col17(undriven), .col18(undriven));
  DotMatrix #(.matrixcols(19), .matrixrows(19)) dotmatrix_11 (
    .col0(main_9_out_2), .col1(main_9_out_6), .col2(main_9_out_10), .col3(main_9_out_14),
    .col4(main_9_out_18), .col5(main_9_out_3), .col6(main_9_out_7), .col7(main_9_out_11),
    .col8(main_9_out_15), .col9(main_9_out_19), .col10(main_9_out_4), .col11(main_9_out_8),
    .col12(main_9_out_12), .col13(main_9_out_16), .col14(main_9_out_20), .col15(main_9_out_5),
    .col16(main_9_out_9), .col17(main_9_out_13), .col18(main_9_out_17));
  number_picker_main main_9 (
    .in_1(_2_o), .out_2(main_9_out_2), .out_3(main_9_out_3), .out_4(main_9_out_4), .out_5(main_9_out_5),
    .out_6(main_9_out_6), .out_7(main_9_out_7), .out_8(main_9_out_8), .out_9(main_9_out_9),
    .out_10(main_9_out_10), .out_11(main_9_out_11), .out_12(main_9_out_12), .out_13(main_9_out_13),
    .out_14(main_9_out_14), .out_15(main_9_out_15), .out_16(main_9_out_16), .out_17(main_9_out_17),
    .out_18(main_9_out_18), .out_19(main_9_out_19), .out_20(main_9_out_20));
  DotMatrix #(.matrixcols(19), .matrixrows(19)) dotmatrix_12 (
    .col0(main_10_out_2), .col1(main_10_out_6), .col2(main_10_out_10), .col3(main_10_out_14),
    .col4(main_10_out_18), .col5(main_10_out_3), .col6(main_10_out_7), .col7(main_10_out_11),
    .col8(main_10_out_15), .col9(main_10_out_19), .col10(main_10_out_4), .col11(main_10_out_8),
    .col12(main_10_out_12), .col13(main_10_out_16), .col14(main_10_out_20), .col15(main_10_out_5),
    .col16(main_10_out_9), .col17(main_10_out_13), .col18(main_10_out_17));
  number_picker_main main_10 (
    .in_1(_6_o), .out_2(main_10_out_2), .out_3(main_10_out_3), .out_4(main_10_out_4), .out_5(main_10_out_5),
    .out_6(main_10_out_6), .out_7(main_10_out_7), .out_8(main_10_out_8), .out_9(main_10_out_9),
    .out_10(main_10_out_10), .out_11(main_10_out_11), .out_12(main_10_out_12), .out_13(main_10_out_13),
    .out_14(main_10_out_14), .out_15(main_10_out_15), .out_16(main_10_out_16), .out_17(main_10_out_17),
    .out_18(main_10_out_18), .out_19(main_10_out_19), .out_20(main_10_out_20));
  DotMatrix #(.matrixcols(19), .matrixrows(19)) dotmatrix_13 (
    .col0(main_11_out_2), .col1(main_11_out_6), .col2(main_11_out_10), .col3(main_11_out_14),
    .col4(main_11_out_18), .col5(main_11_out_3), .col6(main_11_out_7), .col7(main_11_out_11),
    .col8(main_11_out_15), .col9(main_11_out_19), .col10(main_11_out_4), .col11(main_11_out_8),
    .col12(main_11_out_12), .col13(main_11_out_16), .col14(main_11_out_20), .col15(main_11_out_5),
    .col16(main_11_out_9), .col17(main_11_out_13), .col18(main_11_out_17));
  number_picker_main main_11 (
    .in_1(_10_o), .out_2(main_11_out_2), .out_3(main_11_out_3), .out_4(main_11_out_4), .out_5(main_11_out_5),
    .out_6(main_11_out_6), .out_7(main_11_out_7), .out_8(main_11_out_8), .out_9(main_11_out_9),
    .out_10(main_11_out_10), .out_11(main_11_out_11), .out_12(main_11_out_12), .out_13(main_11_out_13),
    .out_14(main_11_out_14), .out_15(main_11_out_15), .out_16(main_11_out_16), .out_17(main_11_out_17),
    .out_18(main_11_out_18), .out_19(main_11_out_19), .out_20(main_11_out_20));
  DotMatrix #(.matrixcols(19), .matrixrows(19)) dotmatrix_14 (
    .col0(main_12_out_2), .col1(main_12_out_6), .col2(main_12_out_10), .col3(main_12_out_14),
    .col4(main_12_out_18), .col5(main_12_out_3), .col6(main_12_out_7), .col7(main_12_out_11),
    .col8(main_12_out_15), .col9(main_12_out_19), .col10(main_12_out_4), .col11(main_12_out_8),
    .col12(main_12_out_12), .col13(main_12_out_16), .col14(main_12_out_20), .col15(main_12_out_5),
    .col16(main_12_out_9), .col17(main_12_out_13), .col18(main_12_out_17));
  number_picker_main main_12 (
    .out_2(main_12_out_2), .out_3(main_12_out_3), .out_4(main_12_out_4), .out_5(main_12_out_5),
    .out_6(main_12_out_6), .out_7(main_12_out_7), .out_8(main_12_out_8), .out_9(main_12_out_9),
    .out_10(main_12_out_10), .out_11(main_12_out_11), .out_12(main_12_out_12), .out_13(main_12_out_13),
    .out_14(main_12_out_14), .out_15(main_12_out_15), .out_16(main_12_out_16), .out_17(main_12_out_17),
    .out_18(main_12_out_18), .out_19(main_12_out_19), .out_20(main_12_out_20));  // open: in_1
  number_picker_main main_13 (
    .in_1(_3_o), .out_2(main_13_out_2), .out_3(main_13_out_3), .out_4(main_13_out_4), .out_5(main_13_out_5),
    .out_6(main_13_out_6), .out_7(main_13_out_7), .out_8(main_13_out_8), .out_9(main_13_out_9),
    .out_10(main_13_out_10), .out_11(main_13_out_11), .out_12(main_13_out_12), .out_13(main_13_out_13),
    .out_14(main_13_out_14), .out_15(main_13_out_15), .out_16(main_13_out_16), .out_17(main_13_out_17),
    .out_18(main_13_out_18), .out_19(main_13_out_19), .out_20(main_13_out_20));
  DotMatrix #(.matrixcols(19), .matrixrows(19)) dotmatrix_15 (
    .col0(main_13_out_2), .col1(main_13_out_6), .col2(main_13_out_10), .col3(main_13_out_14),
    .col4(main_13_out_18), .col5(main_13_out_3), .col6(main_13_out_7), .col7(main_13_out_11),
    .col8(main_13_out_15), .col9(main_13_out_19), .col10(main_13_out_4), .col11(main_13_out_8),
    .col12(main_13_out_12), .col13(main_13_out_16), .col14(main_13_out_20), .col15(main_13_out_5),
    .col16(main_13_out_9), .col17(main_13_out_13), .col18(main_13_out_17));
  number_picker_main main_14 (
    .in_1(_7_o), .out_2(main_14_out_2), .out_3(main_14_out_3), .out_4(main_14_out_4), .out_5(main_14_out_5),
    .out_6(main_14_out_6), .out_7(main_14_out_7), .out_8(main_14_out_8), .out_9(main_14_out_9),
    .out_10(main_14_out_10), .out_11(main_14_out_11), .out_12(main_14_out_12), .out_13(main_14_out_13),
    .out_14(main_14_out_14), .out_15(main_14_out_15), .out_16(main_14_out_16), .out_17(main_14_out_17),
    .out_18(main_14_out_18), .out_19(main_14_out_19), .out_20(main_14_out_20));
  DotMatrix #(.matrixcols(19), .matrixrows(19)) dotmatrix_16 (
    .col0(main_14_out_2), .col1(main_14_out_6), .col2(main_14_out_10), .col3(main_14_out_14),
    .col4(main_14_out_18), .col5(main_14_out_3), .col6(main_14_out_7), .col7(main_14_out_11),
    .col8(main_14_out_15), .col9(main_14_out_19), .col10(main_14_out_4), .col11(main_14_out_8),
    .col12(main_14_out_12), .col13(main_14_out_16), .col14(main_14_out_20), .col15(main_14_out_5),
    .col16(main_14_out_9), .col17(main_14_out_13), .col18(main_14_out_17));
  number_picker_main main_15 (
    .in_1(_11_o), .out_2(main_15_out_2), .out_3(main_15_out_3), .out_4(main_15_out_4), .out_5(main_15_out_5),
    .out_6(main_15_out_6), .out_7(main_15_out_7), .out_8(main_15_out_8), .out_9(main_15_out_9),
    .out_10(main_15_out_10), .out_11(main_15_out_11), .out_12(main_15_out_12), .out_13(main_15_out_13),
    .out_14(main_15_out_14), .out_15(main_15_out_15), .out_16(main_15_out_16), .out_17(main_15_out_17),
    .out_18(main_15_out_18), .out_19(main_15_out_19), .out_20(main_15_out_20));
  DotMatrix #(.matrixcols(19), .matrixrows(19)) dotmatrix_17 (
    .col0(main_15_out_2), .col1(main_15_out_6), .col2(main_15_out_10), .col3(main_15_out_14),
    .col4(main_15_out_18), .col5(main_15_out_3), .col6(main_15_out_7), .col7(main_15_out_11),
    .col8(main_15_out_15), .col9(main_15_out_19), .col10(main_15_out_4), .col11(main_15_out_8),
    .col12(main_15_out_12), .col13(main_15_out_16), .col14(main_15_out_20), .col15(main_15_out_5),
    .col16(main_15_out_9), .col17(main_15_out_13), .col18(main_15_out_17));
  number_picker_main main_16 (
    .out_2(main_16_out_2), .out_3(main_16_out_3), .out_4(main_16_out_4), .out_5(main_16_out_5),
    .out_6(main_16_out_6), .out_7(main_16_out_7), .out_8(main_16_out_8), .out_9(main_16_out_9),
    .out_10(main_16_out_10), .out_11(main_16_out_11), .out_12(main_16_out_12), .out_13(main_16_out_13),
    .out_14(main_16_out_14), .out_15(main_16_out_15), .out_16(main_16_out_16), .out_17(main_16_out_17),
    .out_18(main_16_out_18), .out_19(main_16_out_19), .out_20(main_16_out_20));  // open: in_1
  DotMatrix #(.matrixcols(19), .matrixrows(19)) dotmatrix_18 (
    .col0(main_16_out_2), .col1(main_16_out_6), .col2(main_16_out_10), .col3(main_16_out_14),
    .col4(main_16_out_18), .col5(main_16_out_3), .col6(main_16_out_7), .col7(main_16_out_11),
    .col8(main_16_out_15), .col9(main_16_out_19), .col10(main_16_out_4), .col11(main_16_out_8),
    .col12(main_16_out_12), .col13(main_16_out_16), .col14(main_16_out_20), .col15(main_16_out_5),
    .col16(main_16_out_9), .col17(main_16_out_13), .col18(main_16_out_17));
  Button button_1 ();  // open: out
  Button button_2 ();  // open: out
  Button button_3 ();  // open: out
  Button button_4 ();  // open: out

  // Other names for the same wires on the sheet: RAM[15:0] = data_bus

  // Notes on the sheet:
  //   Garvard architecture
  //   instructions memory
  //   there should be img-file
  //   data memory
  //   workspace
  //   счет
  //   сколько у нас памяти?
  //   как это стыкуется с процессором
  //   CONTROL PANEL
  //   (maybe make  a scheme for that)
endmodule

module random (
  input  in_1,
  output [15:0] out_2
);

  Random #(.width(4)) random_1 (.clk(in_1), .out(out_2[3:0]));  // open: next, clr

  assign out_2[15:4] = {12{1'b0}};
endmodule

module small_comparator (
  input  [3:0] in_1,
  input  [3:0] in_2,
  output out_3
);

  Comparator #(.width(4)) comparator_1 (.a(in_1), .b(in_2), .eq(out_3));  // open: gt, lt
endmodule
