// Logisim project number_picker.circ as structural Verilog: 1 circuit, main circuit main
module main (
  input  [3:0] in_1,
  output [18:0] out_2,
  output [18:0] out_3,
  output [18:0] out_4,
  output [18:0] out_5,
  output [18:0] out_6,
  output [18:0] out_7,
  output [18:0] out_8,
  output [18:0] out_9,
  output [18:0] out_10,
  output [18:0] out_11,
  output [18:0] out_12,
  output [18:0] out_13,
  output [18:0] out_14,
  output [18:0] out_15,
  output [18:0] out_16,
  output [18:0] out_17,
  output [18:0] out_18,
  output [18:0] out_19,
  output [18:0] out_20
);

  wire [18:0] _0_0, _0_1, _0_2, _0_3, _0_4, _0_5, _0_6, _0_7, _0_8, _0_9, _0_10, _0_11, _0_12, _0_13, _0_14,
       _0_15, _0_16, _0_17, _0_18, _1_0, _1_1, _1_2, _1_3, _1_4, _1_5, _1_6, _1_7, _1_8, _1_9, _1_10, _1_11,
       _1_12, _1_13, _1_14, _1_15, _1_16, _1_17, _1_18, _2_0, _2_1, _2_2, _2_3, _2_4, _2_5, _2_6, _2_7, _2_8,
       _2_9, _2_10, _2_11, _2_12, _2_13, _2_14, _2_15, _2_16, _2_17, _2_18, _3_0, _3_1, _3_2, _3_3, _3_4,
       _3_5, _3_6, _3_7, _3_8, _3_9, _3_10, _3_11, _3_12, _3_13, _3_14, _3_15, _3_16, _3_17, _3_18, _4_0,
       _4_1, _4_2, _4_3, _4_4, _4_5, _4_6, _4_7, _4_8, _4_9, _4_10, _4_11, _4_12, _4_13, _4_14, _4_15, _4_16,
       _4_17, _4_18, _5_0, _5_1, _5_2, _5_3, _5_4, _5_5, _5_6, _5_7, _5_8, _5_9, _5_10, _5_11, _5_12, _5_13,
       _5_14, _5_15, _5_16, _5_17, _5_18, _6_0, _6_1, _6_2, _6_3, _6_4, _6_5, _6_6, _6_7, _6_8, _6_9, _6_10,
       _6_11, _6_12, _6_13, _6_14, _6_15, _6_16, _6_17, _6_18, _7_0, _7_1, _7_2, _7_3, _7_4, _7_5, _7_6,
       _7_7, _7_8, _7_9, _7_10, _7_11, _7_12, _7_13, _7_14, _7_15, _7_16, _7_17, _7_18, _8_0, _8_1, _8_2,
       _8_3, _8_4, _8_5, _8_6, _8_7, _8_8, _8_9, _8_10, _8_11, _8_12, _8_13, _8_14, _8_15, _8_16, _8_17,
       _8_18;

  // empty_main main_1: pin names not known; wires that end beside it: _0_0, _0_1, _0_2, _0_3, _0_4, _0_5, _0_6, _0_7, _0_8, _0_9, _0_10, _0_11, _0_12, _0_13, _0_14, _0_15, _0_16
  // _2_main main_2: pin names not known; wires that end beside it: _0_17, _0_18, _1_0, _1_1, _1_2, _1_3, _1_4, _1_5, _1_6, _1_7, _1_8, _1_9, _1_10, _1_11, _1_12, _1_13, _1_14, _1_15, _1_16, _1_17, _1_18
  _4_main main_3 (
    ._4(_2_0), .out_2(_2_1), .out_3(_2_2), .out_4(_2_3), .out_5(_2_4), .out_6(_2_5), .out_7(_2_6),
    .out_8(_2_7), .out_9(_2_8), .out_10(_2_9), .out_11(_2_10), .out_12(_2_11), .out_13(_2_12),
    .out_14(_2_13), .out_15(_2_14), .out_16(_2_15), .out_17(_2_16), .out_18(_2_17), .out_19(_2_18));
  _8_main main_4 (
    ._8(_3_0), .out_2(_3_1), .out_3(_3_2), .out_4(_3_3), .out_5(_3_4), .out_6(_3_5), .out_7(_3_6),
    .out_8(_3_7), .out_9(_3_8), .out_10(_3_9), .out_11(_3_10), .out_12(_3_11), .out_13(_3_12),
    .out_14(_3_13), .out_15(_3_14), .out_16(_3_15), .out_17(_3_16), .out_18(_3_17), .out_19(_3_18));
  _16_main main_5 (
    ._16(_4_0), .out_2(_4_1), .out_3(_4_2), .out_4(_4_3), .out_5(_4_4), .out_6(_4_5), .out_7(_4_6),
    .out_8(_4_7), .out_9(_4_8), .out_10(_4_9), .out_11(_4_10), .out_12(_4_11), .out_13(_4_12),
    .out_14(_4_13), .out_15(_4_14), .out_16(_4_15), .out_17(_4_16), .out_18(_4_17), .out_19(_4_18));
  _32_main main_6 (
    ._32(_5_0), .out_2(_5_1), .out_3(_5_2), .out_4(_5_3), .out_5(_5_4), .out_6(_5_5), .out_7(_5_6),
    .out_8(_5_7), .out_9(_5_8), .out_10(_5_9), .out_11(_5_10), .out_12(_5_11), .out_13(_5_12),
    .out_14(_5_13), .out_15(_5_14), .out_16(_5_15), .out_17(_5_16), .out_18(_5_17), .out_19(_5_18));
  // _64_main main_7: pin names not known; wires that end beside it: _6_0, _6_1, _6_2, _6_3, _6_4, _6_5, _6_6, _6_7, _6_8, _6_9, _6_10, _6_11, _6_12, _6_13, _6_14, _6_15, _6_16, _6_17, _6_18, _7_0, _7_1
  // _128_main main_8: pin names not known; wires that end beside it: _7_2, _7_3, _7_4, _7_5, _7_6, _7_7, _7_8, _7_9
  // _256_main main_9: pin names not known; wires that end beside it: _7_10, _7_11, _7_12, _7_13, _7_14, _7_15, _7_16, _7_17, _7_18, _8_0, _8_1, _8_2, _8_3, _8_4, _8_5, _8_6, _8_7, _8_8, _8_9, _8_10, _8_11, _8_12, _8_13, _8_14, _8_15, _8_16
  // _512_main main_10: pin names not known; wires that end beside it: _8_17, _8_18, _5_0, _5_1, _5_2, _5_3, _5_4, _5_5, _5_6, _5_7, _5_8, _5_9, _5_10, _5_11, _5_12, _5_13, _5_14, _5_15, _5_16, _5_17, _5_18
  _1024_main main_11 (
    ._1024(_5_0), .out_2(_5_1), .out_3(_5_2), .out_4(_5_3), .out_5(_5_4), .out_6(_5_5), .out_7(_5_6),
    .out_8(_5_7), .out_9(_5_8), .out_10(_5_9), .out_11(_5_10), .out_12(_5_11), .out_13(_5_12),
    .out_14(_5_13), .out_15(_5_14), .out_16(_5_15), .out_17(_5_16), .out_18(_5_17), .out_19(_5_18));
  _2048_main main_12 (
    ._2048(_5_0), .out_2(_5_1), .out_3(_5_2), .out_4(_5_3), .out_5(_5_4), .out_6(_5_5), .out_7(_5_6),
    .out_8(_5_7), .out_9(_5_8), .out_10(_5_9), .out_11(_5_10), .out_12(_5_11), .out_13(_5_12),
    .out_14(_5_13), .out_15(_5_14), .out_16(_5_15), .out_17(_5_16), .out_18(_5_17), .out_19(_5_18));
  Multiplexer #(.select(4), .width(19), .enable("false")) multiplexer_1 (
    .in0(_0_0), .in1(_1_0), .in2(_2_0), .in3(_3_0), .out(out_2), .sel(in_1));  // open: in4, in5, in6, in7, in8, in9, in10, in11, in12, in13, in14, in15
  Multiplexer #(.select(4), .width(19), .enable("false")) multiplexer_2 (
    .in0(_0_1), .in1(_1_1), .in2(_2_1), .in3(_3_1), .out(out_6), .sel(in_1));  // open: in4, in5, in6, in7, in8, in9, in10, in11, in12, in13, in14, in15
  Multiplexer #(.select(4), .width(19), .enable("false")) multiplexer_3 (
    .in0(_0_2), .in1(_1_2), .in2(_2_2), .in3(_3_2), .out(out_10), .sel(in_1));  // open: in4, in5, in6, in7, in8, in9, in10, in11, in12, in13, in14, in15
  Multiplexer #(.select(4), .width(19), .enable("false")) multiplexer_4 (
    .in0(_0_3), .in1(_1_3), .in2(_2_3), .in3(_3_3), .out(out_14), .sel(in_1));  // open: in4, in5, in6, in7, in8, in9, in10, in11, in12, in13, in14, in15
  Multiplexer #(.select(4), .width(19), .enable("false")) multiplexer_5 (
    .in0(_0_4), .in1(_1_4), .in2(_2_4), .in3(_3_4), .out(out_18), .sel(in_1));  // open: in4, in5, in6, in7, in8, in9, in10, in11, in12, in13, in14, in15
  Multiplexer #(.select(4), .width(19), .enable("false")) multiplexer_6 (
    .in0(_0_5), .in1(_1_5), .in2(_2_5), .in3(_3_5), .out(out_3), .sel(in_1));  // open: in4, in5, in6, in7, in8, in9, in10, in11, in12, in13, in14, in15
  Multiplexer #(.select(4), .width(19), .enable("false")) multiplexer_7 (
    .in0(_0_6), .in1(_1_6), .in2(_2_6), .in3(_3_6), .out(out_7), .sel(in_1));  // open: in4, in5, in6, in7, in8, in9, in10, in11, in12, in13, in14, in15
  Multiplexer #(.select(4), .width(19), .enable("false")) multiplexer_8 (
    .in0(_0_7), .in1(_1_7), .in2(_2_7), .in3(_3_7), .out(out_11), .sel(in_1));  // open: in4, in5, in6, in7, in8, in9, in10, in11, in12, in13, in14, in15
  Multiplexer #(.select(4), .width(19), .enable("false")) multiplexer_9 (
    .in0(_0_8), .in1(_1_8), .in2(_2_8), .in3(_3_8), .out(out_15), .sel(in_1));  // open: in4, in5, in6, in7, in8, in9, in10, in11, in12, in13, in14, in15
  Multiplexer #(.select(4), .width(19), .enable("false")) multiplexer_10 (
    .in0(_0_9), .in1(_1_9), .in2(_2_9), .in3(_3_9), .out(out_19), .sel(in_1));  // open: in4, in5, in6, in7, in8, in9, in10, in11, in12, in13, in14, in15
  Multiplexer #(.select(4), .width(19), .enable("false")) multiplexer_11 (
    .in0(_0_10), .in1(_1_10), .in2(_2_10), .in3(_3_10), .out(out_4), .sel(in_1));  // open: in4, in5, in6, in7, in8, in9, in10, in11, in12, in13, in14, in15
  Multiplexer #(.select(4), .width(19), .enable("false")) multiplexer_12 (
    .in0(_0_11), .in1(_1_11), .in2(_2_11), .in3(_3_11), .out(out_8), .sel(in_1));  // open: in4, in5, in6, in7, in8, in9, in10, in11, in12, in13, in14, in15
  Multiplexer #(.select(4), .width(19), .enable("false")) multiplexer_13 (
    .in0(_0_12), .in1(_1_12), .in2(_2_12), .in3(_3_12), .out(out_12), .sel(in_1));  // open: in4, in5, in6, in7, in8, in9, in10, in11, in12, in13, in14, in15
  Multiplexer #(.select(4), .width(19), .enable("false")) multiplexer_14 (
    .in0(_0_13), .in1(_1_13), .in2(_2_13), .in3(_3_13), .out(out_16), .sel(in_1));  // open: in4, in5, in6, in7, in8, in9, in10, in11, in12, in13, in14, in15
  Multiplexer #(.select(4), .width(19), .enable("false")) multiplexer_15 (
    .in0(_0_14), .in1(_1_14), .in2(_2_14), .in3(_3_14), .out(out_20), .sel(in_1));  // open: in4, in5, in6, in7, in8, in9, in10, in11, in12, in13, in14, in15
  Multiplexer #(.select(4), .width(19), .enable("false")) multiplexer_16 (
    .in0(_0_15), .in1(_1_15), .in2(_2_15), .in3(_3_15), .out(out_5), .sel(in_1));  // open: in4, in5, in6, in7, in8, in9, in10, in11, in12, in13, in14, in15
  Multiplexer #(.select(4), .width(19), .enable("false")) multiplexer_17 (
    .in0(_0_16), .in1(_1_16), .in2(_2_16), .in3(_3_16), .out(out_9), .sel(in_1));  // open: in4, in5, in6, in7, in8, in9, in10, in11, in12, in13, in14, in15
  Multiplexer #(.select(4), .width(19), .enable("false")) multiplexer_18 (
    .in0(_0_17), .in1(_1_17), .in2(_2_17), .in3(_3_17), .out(out_13), .sel(in_1));  // open: in4, in5, in6, in7, in8, in9, in10, in11, in12, in13, in14, in15
  Multiplexer #(.select(4), .width(19), .enable("false")) multiplexer_19 (
    .in0(_0_18), .in1(_1_18), .in2(_2_18), .in3(_3_18), .out(out_17), .sel(in_1));  // open: in4, in5, in6, in7, in8, in9, in10, in11, in12, in13, in14, in15
endmodule
